# Fritzing sketch Desain Rangkaian (saved by Fritzing 0.8.7b)

parts:
  U4 = ESP8266 NodeMCU LoLin module
  LCM1602_IIC3 = LCM1602 IIC [part_number="LCM1602 IIC" chip_label="LCM1602 IIC" package="DIP (Dual Inline) [THT]"]
  LCD2 = LCD screen
  J2 = Piezo Speaker
  KF-1 = KF-301 Relay [package=THT]
  DHT1 = Humidity and Temperature Sensor DHT11
  M1 = DC Motor
  S1 = KY-026
  Power_plug1 = Power plug

nets:
  N1: U4.D1, LCM1602_IIC3.SDA
  N2: U4.D2, LCM1602_IIC3.SCL
  N3: U4.D3, KF-1.signal
  N4: U4.D4, S1.pin4
  3V3: U4.3V3, DHT1.Vcc, S1.pin3
  GND: U4.GND, LCM1602_IIC3.GND, J2.pin1, KF-1.ground, DHT1.GND_1, M1.pin_1, S1.pin2, Power_plug1.GND
  N5: U4.D5, DHT1.Data-signal
  VIN: U4.Vin, LCM1602_IIC3.VCC, KF-1.C
  N6: U4.SK, J2.pin2
  N7: U4.VU, KF-1.power, Power_plug1.VCC
  VSS: LCM1602_IIC3.VSS, LCD2.VSS
  VDD: LCM1602_IIC3.VDD, LCD2.VDD
  N8: LCM1602_IIC3.V0, LCD2.V0
  N9: LCM1602_IIC3.RS, LCD2.RS
  N10: LCM1602_IIC3.RW, LCD2.R/W
  N11: LCM1602_IIC3.E, LCD2.E
  N12: LCM1602_IIC3.D0, LCD2.DB0
  N13: LCM1602_IIC3.D1, LCD2.DB1
  N14: LCM1602_IIC3.D2, LCD2.DB2
  N15: LCM1602_IIC3.D3, LCD2.DB3
  N16: LCM1602_IIC3.D4, LCD2.DB4
  N17: LCM1602_IIC3.D5, LCD2.DB5
  N18: LCM1602_IIC3.D6, LCD2.DB6
  N19: LCM1602_IIC3.D7, LCD2.DB7
  N20: LCM1602_IIC3.A, LCD2.LED+
  N21: LCM1602_IIC3.K, LCD2.LED-
  N22: LCM1602_IIC3.LED_A, LCM1602_IIC3.LED_B
  N23: KF-1.NO, M1.pin_2

notes:
  LCD 16X2
  POWER SUPLAY
  BUZZER
  FLAME SENSOR
  MOTOR DC
  RELAY
  DHT11
  ESP8266
  LAPORAN PROYEK MONITORING SUHU DAN KELEMBABAN BERBASIS TELEGRAM

custom parts:
  ESP8266 NodeMCU LoLin module: ESP8266 based NodeMCU
  LCM1602 IIC: I2C-Module to use a 1602 or 2004 LCD on with the wire.h libory Serial LCD Modul
  KF-301 Relay: KF-301
  Humidity and Temperature Sensor DHT11: Digital relative humidity & temperature sensor DHT11
  KY-026: ky-026 flame sensor module
